# Fritzing sketch Untitled Sketch (saved by Fritzing 0.9.4)

parts:
  U2 = ESP8266 WiFi Module [part_number=ESP8266]
  U3 = ACS712 [package=so08]
  R5 = Resistor [tolerance=±5% resistance=5k package=THT]
  R6 = Resistor [tolerance=±5% resistance=10k package=THT]
  J1 = Screw terminal - 2 pins [package=THT]
  J2 = Screw terminal - 2 pins [package=THT]
  C1 = Ceramic Capacitor [capacitance=1nF package="100 mil [THT, multilayer]"]
  U4 = RELAY [package=relay-g5q]
  R7 = Resistor [tolerance=±5% resistance=220 package=THT]
  Q1 = NPN-Transistor [package="TO92 [THT]"]
  U5 = Voltage Regulator - 5V [package="TO220 [THT]"]
  HLK-PM1 = HLK-PM01  # not connected

nets:
  N1: U2.VCC, U5.output_voltage
  N2: U2.TXD, R7.Pin_1
  N3: U2.ADC_0, R6.Pin_1
  N4: U3.IP+, J1.pin2
  N5: U3.IP-, U4.NO
  N6: U3.GND, R6.Pin_0
  N7: U3.FILT, C1.0
  N8: U3.VOUT, R5.Pin_0
  N9: J1.pin1, J2.pin2
  N10: J2.pin1, U4.MAIN
  N11: U4.COIL2, U5.input_voltage
  N12: U4.COIL1, Q1.E
  N13: R7.Pin_0, Q1.B
